// Logisim project Dcircuit.circ as structural Verilog: 1 circuit, main circuit main
module main (
  output SRoutput,
  output jkout,
  output dout,
  output tout
);

  wire clock_1_out, D_out, J_out, K_out, R_out, S_out, T_out;

  Clock clock_1 (.out(clock_1_out));
  Clock #(.highDuration(2), .lowDuration(2)) S (.out(S_out));
  Clock #(.highDuration(3), .lowDuration(3)) R (.out(R_out));
  Clock #(.highDuration(2), .lowDuration(2)) J (.out(J_out));
  Clock #(.highDuration(3), .lowDuration(3)) K (.out(K_out));
  Clock #(.highDuration(2), .lowDuration(2)) D (.out(D_out));
  Clock #(.highDuration(2), .lowDuration(2)) T (.out(T_out));
  S_R_Flip_Flop s_r_ff_1 (.S(S_out), .R(R_out), .clk(clock_1_out), .Q(SRoutput));  // open: reset, Qn, preset
  J_K_Flip_Flop j_k_ff_1 (.J(J_out), .K(K_out), .clk(clock_1_out), .Q(jkout));  // open: Qn, preset, reset
  D_Flip_Flop d_ff_1 (.D(D_out), .clk(clock_1_out), .Q(dout));  // open: Qn, preset, reset
  T_Flip_Flop t_ff_1 (.T(T_out), .clk(clock_1_out), .Q(tout));  // open: Qn, reset, preset
  Clock sysclk ();  // open: out
endmodule
