// Logisim project Q3Assignment4.circ as structural Verilog: 1 circuit, main circuit main
module main (
  input  y
);

  wire and_1_out, and_2_out, and_3_out, and_4_out, and_5_out, and_6_out, clock_1_out, not_1_out, not_2_out,
       or_1_out, or_2_out, t_ff_1_q, t_ff_2_q, t_ff_3_q, t_ff_3_qn, xor_1_out, xor_2_out, xor_3_out,
       xor_4_out;

  Clock clock_1 (.out(clock_1_out));
  T_Flip_Flop t_ff_1 (.T(and_5_out), .clk(clock_1_out), .Q(t_ff_1_q));  // open: Qn, reset, preset
  not not_1 (not_1_out, y);
  T_Flip_Flop t_ff_2 (.T(and_6_out), .clk(clock_1_out), .Q(t_ff_2_q));  // open: Qn, reset, preset
  xor xor_1 (xor_1_out, t_ff_1_q, y);
  xor xor_2 (xor_2_out, t_ff_2_q, xor_1_out);
  xor xor_3 (xor_3_out, t_ff_1_q, t_ff_2_q);
  not not_2 (not_2_out, xor_3_out);
  T_Flip_Flop t_ff_3 (.T(xor_4_out), .clk(clock_1_out), .Q(t_ff_3_q), .Qn(t_ff_3_qn));  // open: reset, preset
  and and_1 (and_1_out, xor_3_out, y);
  and and_2 (and_2_out, not_2_out, not_1_out);
  and and_3 (and_3_out, not_1_out, xor_3_out);
  and and_4 (and_4_out, y, not_2_out);
  xor xor_4 (xor_4_out, t_ff_3_q, xor_2_out);
  or or_1 (or_1_out, and_1_out, and_2_out);
  or or_2 (or_2_out, and_3_out, and_4_out);
  and and_5 (and_5_out, t_ff_3_qn, or_1_out);
  and and_6 (and_6_out, t_ff_3_q, or_2_out);
endmodule
