// Logisim project Question2.circ as structural Verilog: 1 circuit, main circuit main
module main (
  input  in_1,
  input  in_2,
  output y
);

  wire and_1_out, clock_out, t_ff_1_q, t_ff_2_q;

  Clock sysclk ();  // open: out
  and and_1 (and_1_out, in_1, t_ff_2_q);
  Clock clock (.out(clock_out));
  T_Flip_Flop t_ff_1 (.T(and_1_out), .clk(clock_out), .Q(t_ff_1_q), .reset(in_2));  // open: Qn, preset
  Clock #(.highDuration(2), .lowDuration(2)) reset (.out(in_2));
  T_Flip_Flop t_ff_2 (.T(in_1), .clk(clock_out), .Q(t_ff_2_q), .reset(in_2));  // open: Qn, preset
  and and_2 (y, t_ff_1_q, t_ff_2_q);
endmodule
