// Logisim project ass2.circ as structural Verilog: 1 circuit, main circuit main
module main (
  input  in_1,
  output out_2
);

  wire and_1_out, and_2_out, clock_1_out, d_ff_1_qn, d_ff_2_q, or_1_out;

  Clock sysclk ();  // open: out
  or or_1 (or_1_out, out_2, d_ff_2_q);
  and and_1 (and_1_out, or_1_out, in_1);
  and and_2 (and_2_out, d_ff_1_qn, in_1);
  D_Flip_Flop d_ff_1 (.D(and_1_out), .clk(clock_1_out), .Q(out_2), .Qn(d_ff_1_qn));  // open: preset, reset
  D_Flip_Flop d_ff_2 (.D(and_2_out), .clk(clock_1_out), .Q(d_ff_2_q));  // open: Qn, preset, reset
  Clock clock_1 (.out(clock_1_out));
endmodule
