// Logisim project counter.circ as structural Verilog: 1 circuit, main circuit main
module main (
);

  wire clock_1_out, clock_2_out, clock_3_out, clock_4_out, d_ff_1_q, d_ff_1_qn, d_ff_2_q, d_ff_2_qn,
       d_ff_3_q, d_ff_3_qn, j_k_ff_3_qn, j_k_ff_4_q, j_k_ff_5_qn, j_k_ff_6_q, t_ff_1_qn, t_ff_2_qn;

  Clock clock_1 (.out(clock_1_out));
  D_Flip_Flop d_ff_1 (.D(d_ff_1_qn), .clk(clock_1_out), .Q(d_ff_1_q), .Qn(d_ff_1_qn));  // open: preset, reset
  T_Flip_Flop t_ff_1 (.T(1'b1), .clk(clock_2_out), .Qn(t_ff_1_qn));  // open: Q, reset, preset
  Clock clock_2 (.out(clock_2_out));
  J_K_Flip_Flop j_k_ff_1 (.J(1'b1), .K(1'b1), .clk(j_k_ff_4_q));  // open: Q, Qn, preset, reset
  J_K_Flip_Flop j_k_ff_2 (.J(1'b1), .K(1'b1), .clk(j_k_ff_3_qn));  // open: Q, Qn, preset, reset
  D_Flip_Flop d_ff_2 (.D(d_ff_2_qn), .clk(d_ff_1_q), .Q(d_ff_2_q), .Qn(d_ff_2_qn));  // open: preset, reset
  J_K_Flip_Flop j_k_ff_3 (.J(1'b1), .K(1'b1), .clk(j_k_ff_5_qn), .Qn(j_k_ff_3_qn));  // open: Q, preset, reset
  T_Flip_Flop t_ff_2 (.T(1'b1), .clk(t_ff_1_qn), .Qn(t_ff_2_qn));  // open: Q, reset, preset
  D_Flip_Flop d_ff_3 (.D(d_ff_3_qn), .clk(d_ff_2_q), .Q(d_ff_3_q), .Qn(d_ff_3_qn));  // open: preset, reset
  J_K_Flip_Flop j_k_ff_4 (.J(1'b1), .K(1'b1), .clk(j_k_ff_6_q), .Q(j_k_ff_4_q));  // open: Qn, preset, reset
  Clock clock_3 (.out(clock_3_out));
  J_K_Flip_Flop j_k_ff_5 (.J(1'b1), .K(1'b1), .clk(clock_4_out), .Qn(j_k_ff_5_qn));  // open: Q, preset, reset
  Clock clock_4 (.out(clock_4_out));
  T_Flip_Flop t_ff_3 (.T(1'b1), .clk(t_ff_2_qn));  // open: Q, Qn, reset, preset
  J_K_Flip_Flop j_k_ff_6 (.J(1'b1), .K(1'b1), .clk(clock_3_out), .Q(j_k_ff_6_q));  // open: Qn, preset, reset
endmodule
