// Logisim project haseeb.circ as structural Verilog: 1 circuit, main circuit main
module main (
);

  wire and_1_out, and_2_out, clock_1_out, j_k_ff_1_qn, j_k_ff_2_q, j_k_ff_3_qn, j_k_ff_4_q;

  Clock clock_1 (.out(clock_1_out));
  J_K_Flip_Flop j_k_ff_1 (.J(and_1_out), .K(1'b1), .clk(clock_1_out), .Qn(j_k_ff_1_qn));  // open: Q, preset, reset
  and and_1 (and_1_out, j_k_ff_2_q, j_k_ff_4_q);
  J_K_Flip_Flop j_k_ff_2 (.J(j_k_ff_1_qn), .K(1'b1), .clk(clock_1_out), .Q(j_k_ff_2_q));  // open: Qn, preset, reset
  J_K_Flip_Flop j_k_ff_3 (.J(1'b1), .K(j_k_ff_2_q), .clk(clock_1_out), .Qn(j_k_ff_3_qn));  // open: Q, preset, reset
  J_K_Flip_Flop j_k_ff_4 (.J(and_2_out), .K(1'b1), .clk(clock_1_out), .Q(j_k_ff_4_q));  // open: Qn, preset, reset
  and and_2 (and_2_out, j_k_ff_3_qn, j_k_ff_1_qn);
endmodule
