// Logisim project lab11counter.circ as structural Verilog: 1 circuit, main circuit main
module main (
  input  in_1,
  input  EN,
  input  in_3,
  input  in_4,
  input  in_5,
  input  in_6
);

  wire and_1_out, and_2_out, and_3_out, and_4_out, clock_1_out, d_ff_1_q, d_ff_2_q, d_ff_3_q, d_ff_4_q,
       multiplexer_1_out, multiplexer_2_out, multiplexer_3_out, multiplexer_4_out, xor_1_out, xor_2_out,
       xor_3_out, xor_4_out;

  // Probe on and_1_out
  and and_1 (and_1_out, and_2_out, d_ff_1_q);
  Clock clock_1 (.out(clock_1_out));
  xor xor_1 (xor_1_out, and_2_out, d_ff_1_q);
  Multiplexer multiplexer_1 (.in0(xor_1_out), .in1(in_4), .out(multiplexer_1_out), .sel(in_1));
  D_Flip_Flop d_ff_1 (.D(multiplexer_1_out), .clk(clock_1_out), .Q(d_ff_1_q));  // open: Qn, preset, reset
  and and_2 (and_2_out, and_3_out, d_ff_2_q);
  xor xor_2 (xor_2_out, d_ff_2_q, and_3_out);
  Multiplexer multiplexer_2 (.in0(xor_2_out), .in1(in_5), .out(multiplexer_2_out), .sel(in_1));
  and and_3 (and_3_out, and_4_out, d_ff_3_q);
  D_Flip_Flop d_ff_2 (.D(multiplexer_2_out), .clk(clock_1_out), .Q(d_ff_2_q));  // open: Qn, preset, reset
  xor xor_3 (xor_3_out, and_4_out, d_ff_3_q);
  Multiplexer multiplexer_3 (.in0(xor_3_out), .in1(in_6), .out(multiplexer_3_out), .sel(in_1));
  and and_4 (and_4_out, EN, d_ff_4_q);
  D_Flip_Flop d_ff_3 (.D(multiplexer_3_out), .clk(clock_1_out), .Q(d_ff_3_q));  // open: Qn, preset, reset
  xor xor_4 (xor_4_out, EN, d_ff_4_q);
  Multiplexer multiplexer_4 (.in0(xor_4_out), .in1(in_3), .out(multiplexer_4_out), .sel(in_1));
  D_Flip_Flop d_ff_4 (.D(multiplexer_4_out), .clk(clock_1_out), .Q(d_ff_4_q));  // open: Qn, preset, reset
endmodule
