// Logisim project loadcounter.circ as structural Verilog: 1 circuit, main circuit main
module main (
  input  in_1,
  input  in_2,
  input  in_3,
  input  in_4,
  input  in_5,
  input  in_6
);

  wire and_2_out, and_3_out, and_4_out, and_5_out, clock_1_out, d_ff_1_q, d_ff_2_q, d_ff_2_qn, d_ff_3_q,
       d_ff_3_qn, d_ff_4_q, multiplexer_1_out, multiplexer_2_out, multiplexer_3_out, multiplexer_4_out,
       or_1_out, xor_1_out, xor_2_out, xor_3_out, xor_4_out;

  or or_1 (or_1_out, in_6, and_2_out);
  // AND_Gate and_1 has open pins: in0=and_3_out, in1=d_ff_1_q, out=open
  Clock clock_1 (.out(clock_1_out));
  and and_2 (and_2_out, d_ff_1_q, d_ff_2_qn, d_ff_3_qn, d_ff_4_q);
  xor xor_1 (xor_1_out, and_3_out, d_ff_1_q);
  Multiplexer #(.enable("false")) multiplexer_1 (.in0(xor_1_out), .in1(in_2), .out(multiplexer_1_out), .sel(or_1_out));
  D_Flip_Flop d_ff_1 (.D(multiplexer_1_out), .clk(clock_1_out), .Q(d_ff_1_q));  // open: Qn, preset, reset
  and and_3 (and_3_out, and_4_out, d_ff_2_q);
  D_Flip_Flop d_ff_2 (.D(multiplexer_2_out), .clk(clock_1_out), .Q(d_ff_2_q), .Qn(d_ff_2_qn));  // open: preset, reset
  xor xor_2 (xor_2_out, d_ff_2_q, and_4_out);
  Multiplexer #(.enable("false")) multiplexer_2 (.in0(xor_2_out), .in1(in_4), .out(multiplexer_2_out), .sel(or_1_out));
  and and_4 (and_4_out, and_5_out, d_ff_3_q);
  xor xor_3 (xor_3_out, d_ff_3_q, and_5_out);
  Multiplexer #(.enable("false")) multiplexer_3 (.in0(xor_3_out), .in1(in_5), .out(multiplexer_3_out), .sel(or_1_out));
  D_Flip_Flop d_ff_3 (.D(multiplexer_3_out), .clk(clock_1_out), .Q(d_ff_3_q), .Qn(d_ff_3_qn));  // open: preset, reset
  and and_5 (and_5_out, d_ff_4_q, in_1);
  D_Flip_Flop d_ff_4 (.D(multiplexer_4_out), .clk(clock_1_out), .Q(d_ff_4_q));  // open: Qn, preset, reset
  xor xor_4 (xor_4_out, in_1, d_ff_4_q);
  Multiplexer #(.enable("false")) multiplexer_4 (.in0(xor_4_out), .in1(in_3), .out(multiplexer_4_out), .sel(or_1_out));
endmodule
