// Logisim project pInSout.circ as structural Verilog: 1 circuit, main circuit main
module main (
  input  in_1,
  input  in_2,
  input  in_3,
  input  Load,
  input  in_5,
  output out_6
);

  wire and_1_out, and_2_out, and_3_out, and_4_out, and_5_out, and_6_out, clock_1_out, not_1_out, or_1_out,
       or_2_out, or_3_out, t_ff_1_q, t_ff_2_q, t_ff_3_q, xor_1_out, xor_2_out, xor_3_out, xor_4_out;

  xor xor_1 (xor_1_out, t_ff_1_q, in_5);
  Clock clock_1 (.out(clock_1_out));
  not not_1 (not_1_out, Load);
  T_Flip_Flop t_ff_1 (.T(xor_1_out), .clk(clock_1_out), .Q(t_ff_1_q));  // open: Qn, reset, preset
  and and_1 (and_1_out, t_ff_1_q, not_1_out);
  or or_1 (or_1_out, and_1_out, and_2_out);
  and and_2 (and_2_out, Load, in_1);
  T_Flip_Flop t_ff_2 (.T(xor_2_out), .clk(clock_1_out), .Q(t_ff_2_q));  // open: Qn, reset, preset
  xor xor_2 (xor_2_out, t_ff_2_q, or_1_out);
  and and_3 (and_3_out, t_ff_2_q, not_1_out);
  and and_4 (and_4_out, Load, in_2);
  or or_2 (or_2_out, and_3_out, and_4_out);
  T_Flip_Flop t_ff_3 (.T(xor_3_out), .clk(clock_1_out), .Q(t_ff_3_q));  // open: Qn, reset, preset
  xor xor_3 (xor_3_out, t_ff_3_q, or_2_out);
  and and_5 (and_5_out, Load, in_3);
  and and_6 (and_6_out, t_ff_3_q, not_1_out);
  or or_3 (or_3_out, and_6_out, and_5_out);
  xor xor_4 (xor_4_out, out_6, or_3_out);
  T_Flip_Flop t_ff_4 (.T(xor_4_out), .clk(clock_1_out), .Q(out_6));  // open: Qn, reset, preset
endmodule
