// Logisim project parallelInParallelOut.circ as structural Verilog: 1 circuit, main circuit main
module main (
  input  in_1,
  input  in_2,
  input  in_3,
  input  in_4,
  output out_5,
  output out_6,
  output out_7,
  output out_8
);

  wire clock_1_out, not_1_out, not_2_out, not_3_out, not_4_out;

  not not_1 (not_1_out, in_3);
  Clock clock_1 (.out(clock_1_out));
  J_K_Flip_Flop j_k_ff_1 (.J(in_3), .K(not_1_out), .clk(clock_1_out), .Q(out_8));  // open: Qn, preset, reset
  J_K_Flip_Flop j_k_ff_2 (.J(in_4), .K(not_2_out), .clk(clock_1_out), .Q(out_6));  // open: Qn, preset, reset
  not not_2 (not_2_out, in_4);
  J_K_Flip_Flop j_k_ff_3 (.J(in_1), .K(not_3_out), .clk(clock_1_out), .Q(out_7));  // open: Qn, preset, reset
  not not_3 (not_3_out, in_1);
  not not_4 (not_4_out, in_2);
  J_K_Flip_Flop j_k_ff_4 (.J(in_2), .K(not_4_out), .clk(clock_1_out), .Q(out_5));  // open: Qn, preset, reset
endmodule
