// Logisim project parallelInSerialOut.circ as structural Verilog: 1 circuit, main circuit main
module main (
  input  in_1,
  input  in_2,
  input  in_3,
  input  Load,
  input  in_5,
  output out_6
);

  wire and_1_out, and_2_out, and_3_out, and_4_out, and_5_out, and_6_out, clock_1_out, j_k_ff_1_q, j_k_ff_2_q,
       j_k_ff_3_q, not_1_out, not_2_out, not_3_out, not_4_out, not_5_out, or_1_out, or_2_out, or_3_out;

  Clock clock_1 (.out(clock_1_out));
  not not_1 (not_1_out, in_5);
  not not_2 (not_2_out, Load);
  J_K_Flip_Flop j_k_ff_1 (.J(in_5), .K(not_1_out), .clk(clock_1_out), .Q(j_k_ff_1_q));  // open: Qn, preset, reset
  and and_1 (and_1_out, j_k_ff_1_q, Load);
  or or_1 (or_1_out, and_1_out, and_2_out);
  J_K_Flip_Flop j_k_ff_2 (.J(or_1_out), .K(not_3_out), .clk(clock_1_out), .Q(j_k_ff_2_q));  // open: Qn, preset, reset
  not not_3 (not_3_out, or_1_out);
  and and_2 (and_2_out, not_2_out, in_1);
  and and_3 (and_3_out, j_k_ff_2_q, Load);
  and and_4 (and_4_out, not_2_out, in_2);
  or or_2 (or_2_out, and_3_out, and_4_out);
  J_K_Flip_Flop j_k_ff_3 (.J(or_2_out), .K(not_4_out), .clk(clock_1_out), .Q(j_k_ff_3_q));  // open: Qn, preset, reset
  not not_4 (not_4_out, or_2_out);
  and and_5 (and_5_out, not_2_out, in_3);
  and and_6 (and_6_out, j_k_ff_3_q, Load);
  or or_3 (or_3_out, and_6_out, and_5_out);
  J_K_Flip_Flop j_k_ff_4 (.J(or_3_out), .K(not_5_out), .clk(clock_1_out), .Q(out_6));  // open: Qn, preset, reset
  not not_5 (not_5_out, or_3_out);
endmodule
