// Logisim project parallelInSerioalOutTflipflop.circ as structural Verilog: 1 circuit, main circuit main
module main (
  input  in_1,
  output out_2,
  output out_3,
  output out_4,
  output out_5
);

  wire clock_1_out, xor_1_out, xor_2_out, xor_3_out, xor_4_out;

  xor xor_1 (xor_1_out, out_2, in_1);
  Clock clock_1 (.out(clock_1_out));
  T_Flip_Flop t_ff_1 (.T(xor_1_out), .clk(clock_1_out), .Q(out_2));  // open: Qn, reset, preset
  T_Flip_Flop t_ff_2 (.T(xor_2_out), .clk(clock_1_out), .Q(out_3));  // open: Qn, reset, preset
  xor xor_2 (xor_2_out, out_3, out_2);
  T_Flip_Flop t_ff_3 (.T(xor_3_out), .clk(clock_1_out), .Q(out_4));  // open: Qn, reset, preset
  xor xor_3 (xor_3_out, out_4, out_3);
  xor xor_4 (xor_4_out, out_5, out_4);
  T_Flip_Flop t_ff_4 (.T(xor_4_out), .clk(clock_1_out), .Q(out_5));  // open: Qn, reset, preset
endmodule
