// Logisim project parallelLoadJK.circ as structural Verilog: 1 circuit, main circuit main
module main (
  input  in_1,
  input  in_2,
  input  in_3,
  input  in_4,
  input  in_5
);

  wire and_1_out, and_2_out, and_3_out, and_4_out, and_5_out, and_6_out, and_7_out, and_8_out, clock_1_out,
       j_k_ff_2_q, j_k_ff_3_q, multiplexer_1_out, multiplexer_2_out, multiplexer_3_out, multiplexer_4_out,
       multiplexer_5_out, multiplexer_6_out, not_1_out, not_2_out, not_3_out;

  and and_1 (and_1_out, j_k_ff_2_q, in_4, j_k_ff_3_q);
  Multiplexer #(.enable("false")) multiplexer_1 (.in0(and_1_out), .in1(and_3_out), .out(multiplexer_1_out), .sel(in_5));
  Multiplexer #(.enable("false")) multiplexer_2 (.in0(and_1_out), .in1(and_2_out), .out(multiplexer_2_out), .sel(in_5));
  not not_1 (not_1_out, in_2);
  and and_2 (and_2_out, not_1_out, in_4);
  Clock clock_1 (.out(clock_1_out));
  and and_3 (and_3_out, in_2, in_4);
  J_K_Flip_Flop j_k_ff_1 (
    .J(multiplexer_1_out), .K(multiplexer_2_out), .clk(clock_1_out));  // open: Q, Qn, preset, reset
  not not_2 (not_2_out, in_3);
  and and_4 (and_4_out, not_2_out, in_4);
  and and_5 (and_5_out, in_4, j_k_ff_3_q);
  Multiplexer #(.enable("false")) multiplexer_3 (.in0(and_5_out), .in1(and_4_out), .out(multiplexer_3_out), .sel(in_5));
  and and_6 (and_6_out, in_3, in_4);
  Multiplexer #(.enable("false")) multiplexer_4 (.in0(and_5_out), .in1(and_6_out), .out(multiplexer_4_out), .sel(in_5));
  J_K_Flip_Flop j_k_ff_2 (
    .J(multiplexer_4_out), .K(multiplexer_3_out), .clk(clock_1_out), .Q(j_k_ff_2_q));  // open: Qn, preset, reset
  not not_3 (not_3_out, in_1);
  Multiplexer #(.enable("false")) multiplexer_5 (.in0(in_4), .in1(and_8_out), .out(multiplexer_5_out), .sel(in_5));
  and and_7 (and_7_out, in_1, in_4);
  and and_8 (and_8_out, not_3_out, in_4);
  Multiplexer #(.enable("false")) multiplexer_6 (.in0(in_4), .in1(and_7_out), .out(multiplexer_6_out), .sel(in_5));
  J_K_Flip_Flop j_k_ff_3 (
    .J(multiplexer_6_out), .K(multiplexer_5_out), .clk(clock_1_out), .Q(j_k_ff_3_q));  // open: Qn, preset, reset
endmodule
