// Logisim project parallelloadcounterjkff.circ as structural Verilog: 1 circuit, main circuit main
module main (
  input  in_1,
  input  in_2,
  input  in_3,
  input  in_4,
  input  in_5
);

  wire and_1_out, and_4_out, clock_1_out, clock_2_out, j_k_ff_3_q, j_k_ff_4_qn, j_k_ff_5_q, j_k_ff_6_qn;

  Clock clock_1 (.out(clock_1_out));
  and and_1 (and_1_out, in_1, j_k_ff_5_q, j_k_ff_3_q);
  J_K_Flip_Flop j_k_ff_1 (.J(and_1_out), .K(and_1_out), .clk(clock_1_out));  // open: Q, Qn, preset, reset
  // AND_Gate and_2 has open pins: in1=in_5, out=open
  J_K_Flip_Flop j_k_ff_2 (.J(1'b1), .K(1'b1), .clk(j_k_ff_4_qn));  // open: Q, Qn, preset, reset
  J_K_Flip_Flop j_k_ff_3 (.J(and_4_out), .K(and_4_out), .clk(clock_1_out), .Q(j_k_ff_3_q));  // open: Qn, preset, reset
  // AND_Gate and_3 has open pins: in1=in_5, out=open
  J_K_Flip_Flop j_k_ff_4 (.J(1'b1), .K(1'b1), .clk(j_k_ff_6_qn), .Qn(j_k_ff_4_qn));  // open: Q, preset, reset
  and and_4 (and_4_out, j_k_ff_5_q, in_1);
  J_K_Flip_Flop j_k_ff_5 (.J(in_1), .K(in_1), .clk(clock_1_out), .Q(j_k_ff_5_q));  // open: Qn, preset, reset
  // AND_Gate and_5 has open pins: in1=in_5, out=open
  J_K_Flip_Flop j_k_ff_6 (.J(1'b1), .K(1'b1), .clk(clock_2_out), .Qn(j_k_ff_6_qn));  // open: Q, preset, reset
  Clock clock_2 (.out(clock_2_out));
endmodule
