// Logisim project prac.circ as structural Verilog: 1 circuit, main circuit main
module main (
);

  wire and_1_out, clock_1_out, clock_2_out, clock_3_out, d_ff_1_qn, d_ff_2_q, d_ff_2_qn, d_ff_3_qn, d_ff_4_q,
       d_ff_4_qn, j_k_ff_1_qn, j_k_ff_2_qn, t_ff_1_qn, t_ff_2_qn;

  Clock clock_1 (.out(clock_1_out));
  Clock clock_2 (.out(clock_2_out));
  T_Flip_Flop t_ff_1 (.T(1'b1), .clk(clock_3_out), .Qn(t_ff_1_qn));  // open: Q, reset, preset
  Clock clock_3 (.out(clock_3_out));
  D_Flip_Flop d_ff_1 (.D(d_ff_1_qn), .clk(clock_1_out), .Qn(d_ff_1_qn), .reset(and_1_out));  // open: Q, preset
  J_K_Flip_Flop j_k_ff_1 (.J(1'b1), .K(1'b1), .clk(clock_2_out), .Qn(j_k_ff_1_qn));  // open: Q, preset, reset
  T_Flip_Flop t_ff_2 (.T(1'b1), .clk(t_ff_1_qn), .Qn(t_ff_2_qn));  // open: Q, reset, preset
  D_Flip_Flop d_ff_2 (.D(d_ff_2_qn), .clk(d_ff_1_qn), .Q(d_ff_2_q), .Qn(d_ff_2_qn), .reset(and_1_out));  // open: preset
  J_K_Flip_Flop j_k_ff_2 (.J(1'b1), .K(1'b1), .clk(j_k_ff_1_qn), .Qn(j_k_ff_2_qn));  // open: Q, preset, reset
  and and_1 (and_1_out, d_ff_2_q, d_ff_3_qn, d_ff_1_qn, d_ff_4_q);
  T_Flip_Flop t_ff_3 (.T(1'b1), .clk(t_ff_2_qn));  // open: Q, Qn, reset, preset
  D_Flip_Flop d_ff_3 (.D(d_ff_3_qn), .clk(d_ff_2_qn), .Qn(d_ff_3_qn), .reset(and_1_out));  // open: Q, preset
  J_K_Flip_Flop j_k_ff_3 (.J(1'b1), .K(1'b1), .clk(j_k_ff_2_qn));  // open: Q, Qn, preset, reset
  D_Flip_Flop d_ff_4 (.D(d_ff_4_qn), .clk(d_ff_3_qn), .Q(d_ff_4_q), .Qn(d_ff_4_qn), .reset(and_1_out));  // open: preset
endmodule
