// Logisim project q1Tflipass4.circ as structural Verilog: 1 circuit, main circuit main
module main (
  input  in_1,
  input  in_2,
  input  in_3,
  input  in_4,
  output out_5,
  output out_6,
  output out_7,
  output out_8
);

  wire clock_1_out, xor_1_out, xor_2_out, xor_3_out, xor_4_out;

  Clock clock_1 (.out(clock_1_out));
  T_Flip_Flop t_ff_1 (.T(xor_1_out), .clk(clock_1_out), .Q(out_6));  // open: Qn, reset, preset
  xor xor_1 (xor_1_out, out_6, in_2);
  T_Flip_Flop t_ff_2 (.T(xor_2_out), .clk(clock_1_out), .Q(out_7));  // open: Qn, reset, preset
  xor xor_2 (xor_2_out, out_7, in_1);
  T_Flip_Flop t_ff_3 (.T(xor_3_out), .clk(clock_1_out), .Q(out_8));  // open: Qn, reset, preset
  xor xor_3 (xor_3_out, in_3, out_8);
  T_Flip_Flop t_ff_4 (.T(xor_4_out), .clk(clock_1_out), .Q(out_5));  // open: Qn, reset, preset
  xor xor_4 (xor_4_out, out_5, in_4);
endmodule
