// Logisim project q2.circ as structural Verilog: 1 circuit, main circuit main
module main (
  input  in_1,
  output out_2
);

  wire clock_1_out, j_k_ff_1_qn, j_k_ff_2_q, j_k_ff_2_qn, nand_1_out, nand_2_out, nand_3_out, not_1_out,
       not_2_out;

  Clock sysclk ();  // open: out
  not not_1 (not_1_out, in_1);
  nand nand_1 (nand_1_out, in_1, j_k_ff_2_qn);
  nand nand_2 (nand_2_out, j_k_ff_2_q, not_1_out);
  nand nand_3 (nand_3_out, nand_1_out, nand_2_out);
  not not_2 (not_2_out, nand_2_out);
  J_K_Flip_Flop j_k_ff_1 (
    .J(nand_3_out), .K(not_2_out), .clk(clock_1_out), .Qn(j_k_ff_1_qn));  // open: Q, preset, reset
  J_K_Flip_Flop j_k_ff_2 (
    .J(not_1_out), .K(not_1_out), .clk(clock_1_out), .Q(j_k_ff_2_q), .Qn(j_k_ff_2_qn));  // open: preset, reset
  Clock clock_1 (.out(clock_1_out));
  nor nor_1 (out_2, j_k_ff_1_qn, j_k_ff_2_qn);
endmodule
