// Logisim project question4ass5.circ as structural Verilog: 1 circuit, main circuit main
module main (
  input  in_1
);

  wire and_1_out, and_2_out, and_3_out, and_4_out, and_5_out, and_6_out, clock_1_out, not_1_out, or_1_out,
       or_2_out, or_3_out, or_4_out, or_5_out, t_ff_1_q, t_ff_1_qn, t_ff_2_q, t_ff_2_qn, t_ff_3_q, t_ff_3_qn,
       xor_1_out, xor_2_out;

  not not_1 (not_1_out, in_1);
  and and_1 (and_1_out, not_1_out, t_ff_1_q, t_ff_2_qn, t_ff_3_qn);
  and and_2 (and_2_out, in_1, t_ff_1_qn, t_ff_2_q, t_ff_3_q);
  T_Flip_Flop t_ff_1 (.T(or_1_out), .clk(clock_1_out), .Q(t_ff_1_q), .Qn(t_ff_1_qn));  // open: reset, preset
  Clock clock_1 (.out(clock_1_out));
  or or_1 (or_1_out, and_1_out, and_2_out);
  or or_2 (or_2_out, t_ff_2_q, t_ff_1_q);
  T_Flip_Flop t_ff_2 (.T(or_4_out), .clk(clock_1_out), .Q(t_ff_2_q), .Qn(t_ff_2_qn));  // open: reset, preset
  and and_3 (and_3_out, not_1_out, t_ff_3_qn, or_2_out);
  or or_3 (or_3_out, t_ff_1_qn, t_ff_2_qn);
  and and_4 (and_4_out, in_1, t_ff_3_q, or_3_out);
  T_Flip_Flop t_ff_3 (.T(or_5_out), .clk(clock_1_out), .Q(t_ff_3_q), .Qn(t_ff_3_qn));  // open: reset, preset
  xor xor_1 (xor_1_out, in_1, t_ff_1_q);
  xor xor_2 (xor_2_out, t_ff_2_q, t_ff_3_q);
  or or_4 (or_4_out, and_3_out, and_4_out);
  and and_5 (and_5_out, t_ff_2_qn, in_1);
  and and_6 (and_6_out, t_ff_3_q, not_1_out);
  or or_5 (or_5_out, and_5_out, and_6_out, xor_1_out, xor_2_out);
endmodule
