// Logisim project quiz.circ as structural Verilog: 1 circuit, main circuit main
module main (
);

  wire and_1_out, and_2_out, and_3_out, and_4_out, and_5_out, clock_1_out, clock_2_out, d_ff_1_q, d_ff_1_qn,
       d_ff_2_q, d_ff_2_qn, d_ff_3_q, j_k_ff_1_q, j_k_ff_2_q, j_k_ff_3_qn, or_1_out, or_2_out, or_3_out;

  and and_1 (and_1_out, d_ff_2_q, d_ff_3_q);
  Clock clock_1 (.out(clock_1_out));
  Clock clock_2 (.out(clock_2_out));
  D_Flip_Flop d_ff_1 (.D(or_1_out), .clk(clock_1_out), .Q(d_ff_1_q), .Qn(d_ff_1_qn));  // open: preset, reset
  or or_1 (or_1_out, d_ff_1_qn, and_1_out);
  J_K_Flip_Flop j_k_ff_1 (.J(1'b1), .K(j_k_ff_3_qn), .clk(clock_2_out), .Q(j_k_ff_1_q));  // open: Qn, preset, reset
  and and_2 (and_2_out, d_ff_1_q, d_ff_2_qn);
  D_Flip_Flop d_ff_2 (.D(or_2_out), .clk(clock_1_out), .Q(d_ff_2_q), .Qn(d_ff_2_qn));  // open: preset, reset
  J_K_Flip_Flop j_k_ff_2 (.J(1'b1), .K(j_k_ff_1_q), .clk(clock_2_out), .Q(j_k_ff_2_q));  // open: Qn, preset, reset
  or or_2 (or_2_out, and_2_out, d_ff_1_qn);
  and and_3 (and_3_out, d_ff_1_q, d_ff_2_q);
  and and_4 (and_4_out, d_ff_3_q, d_ff_1_qn);
  and and_5 (and_5_out, j_k_ff_2_q, j_k_ff_1_q);
  J_K_Flip_Flop j_k_ff_3 (
    .J(and_5_out), .K(j_k_ff_1_q), .clk(clock_2_out), .Qn(j_k_ff_3_qn));  // open: Q, preset, reset
  D_Flip_Flop d_ff_3 (.D(or_3_out), .clk(clock_1_out), .Q(d_ff_3_q));  // open: Qn, preset, reset
  or or_3 (or_3_out, and_3_out, and_4_out);
endmodule
