// Logisim project quiz6.circ as structural Verilog: 1 circuit, main circuit main
module main (
  input  in_1,
  output out_2
);

  wire and_1_out, and_2_out, and_3_out, and_4_out, and_5_out, and_6_out, and_7_out, and_8_out, clock_1_out,
       not_1_out, or_1_out, or_2_out, t_ff_1_q, t_ff_1_qn, t_ff_2_q, t_ff_3_q, t_ff_3_qn, xor_1_out;

  not not_1 (not_1_out, in_1);
  and and_1 (and_1_out, not_1_out, t_ff_1_q, t_ff_3_qn);
  and and_2 (and_2_out, t_ff_2_q, t_ff_3_q);
  or or_1 (or_1_out, and_1_out, and_2_out);
  T_Flip_Flop t_ff_1 (.T(or_1_out), .clk(clock_1_out), .Q(t_ff_1_q), .Qn(t_ff_1_qn));  // open: reset, preset
  Clock clock_1 (.out(clock_1_out));
  and and_3 (and_3_out, not_1_out, t_ff_3_q);
  and and_4 (and_4_out, t_ff_1_q, t_ff_2_q);
  and and_5 (and_5_out, t_ff_1_qn, t_ff_3_q);
  and and_6 (and_6_out, not_1_out, t_ff_2_q);
  T_Flip_Flop t_ff_2 (.T(or_2_out), .clk(clock_1_out), .Q(t_ff_2_q));  // open: Qn, reset, preset
  or or_2 (or_2_out, and_3_out, and_4_out, and_5_out, and_6_out);
  T_Flip_Flop t_ff_3 (.T(xor_1_out), .clk(clock_1_out), .Q(t_ff_3_q), .Qn(t_ff_3_qn));  // open: reset, preset
  xor xor_1 (xor_1_out, in_1, t_ff_3_q);
  and and_7 (and_7_out, in_1, t_ff_3_q);
  and and_8 (and_8_out, in_1, t_ff_1_q, t_ff_2_q);
  or or_3 (out_2, and_7_out, and_8_out);
endmodule
