// Logisim project qustion3assignment5.circ as structural Verilog: 1 circuit, main circuit main
module main (
  input  in_1,
  input  Enable,
  input  in_3,
  input  in_4,
  input  in_5,
  input  in_6,
  input  in_7,
  input  in_8,
  input  in_9
);

  wire and_2_out, and_3_out, and_4_out, and_5_out, and_6_out, and_7_out, and_8_out, clock_1_out, d_ff_1_q,
       d_ff_2_q, d_ff_3_q, d_ff_4_q, d_ff_5_q, d_ff_6_q, d_ff_7_q, multiplexer_1_out, multiplexer_2_out,
       multiplexer_3_out, multiplexer_4_out, multiplexer_5_out, multiplexer_6_out, multiplexer_7_out,
       not_1_out, or_1_out, xor_1_out, xor_2_out, xor_3_out, xor_4_out, xor_5_out, xor_6_out, xor_7_out;

  // AND_Gate and_1 has open pins: in0=and_2_out, in1=d_ff_1_q, out=open
  not not_1 (not_1_out, or_1_out);
  Clock clock_1 (.out(clock_1_out));
  xor xor_1 (xor_1_out, and_2_out, d_ff_1_q);
  Multiplexer #(.enable("false")) multiplexer_1 (.in0(in_5), .in1(xor_1_out), .out(multiplexer_1_out), .sel(not_1_out));
  D_Flip_Flop d_ff_1 (.D(multiplexer_1_out), .clk(clock_1_out), .Q(d_ff_1_q));  // open: Qn, preset, reset
  or or_1 (or_1_out, in_9, and_3_out);
  and and_2 (and_2_out, and_4_out, d_ff_2_q);
  xor xor_2 (xor_2_out, d_ff_2_q, and_4_out);
  Multiplexer #(.enable("false")) multiplexer_2 (.in0(in_6), .in1(xor_2_out), .out(multiplexer_2_out), .sel(not_1_out));
  and and_3 (and_3_out, d_ff_1_q, d_ff_2_q);
  D_Flip_Flop d_ff_2 (.D(multiplexer_2_out), .clk(clock_1_out), .Q(d_ff_2_q));  // open: Qn, preset, reset
  and and_4 (and_4_out, and_5_out, d_ff_3_q);
  and and_5 (and_5_out, and_6_out, d_ff_4_q);
  xor xor_3 (xor_3_out, and_5_out, d_ff_3_q);
  Multiplexer #(.enable("false")) multiplexer_3 (.in0(in_7), .in1(xor_3_out), .out(multiplexer_3_out), .sel(not_1_out));
  D_Flip_Flop d_ff_3 (.D(multiplexer_3_out), .clk(clock_1_out), .Q(d_ff_3_q));  // open: Qn, preset, reset
  xor xor_4 (xor_4_out, and_6_out, d_ff_4_q);
  Multiplexer #(.enable("false")) multiplexer_4 (.in0(in_8), .in1(xor_4_out), .out(multiplexer_4_out), .sel(not_1_out));
  D_Flip_Flop d_ff_4 (.D(multiplexer_4_out), .clk(clock_1_out), .Q(d_ff_4_q));  // open: Qn, preset, reset
  and and_6 (and_6_out, and_7_out, d_ff_5_q);
  and and_7 (and_7_out, and_8_out, d_ff_6_q);
  xor xor_5 (xor_5_out, and_7_out, d_ff_5_q);
  Multiplexer #(.enable("false")) multiplexer_5 (.in0(in_3), .in1(xor_5_out), .out(multiplexer_5_out), .sel(not_1_out));
  D_Flip_Flop d_ff_5 (.D(multiplexer_5_out), .clk(clock_1_out), .Q(d_ff_5_q));  // open: Qn, preset, reset
  Multiplexer #(.enable("false")) multiplexer_6 (.in0(in_4), .in1(xor_6_out), .out(multiplexer_6_out), .sel(not_1_out));
  and and_8 (and_8_out, Enable, d_ff_7_q);
  xor xor_6 (xor_6_out, and_8_out, d_ff_6_q);
  D_Flip_Flop d_ff_6 (.D(multiplexer_6_out), .clk(clock_1_out), .Q(d_ff_6_q));  // open: Qn, preset, reset
  Multiplexer #(.enable("false")) multiplexer_7 (.in0(in_1), .in1(xor_7_out), .out(multiplexer_7_out), .sel(not_1_out));
  D_Flip_Flop d_ff_7 (.D(multiplexer_7_out), .clk(clock_1_out), .Q(d_ff_7_q));  // open: Qn, preset, reset
  xor xor_7 (xor_7_out, Enable, d_ff_7_q);
endmodule
