// Logisim project serialInOut.circ as structural Verilog: 1 circuit, main circuit main
module main (
  input  in_1,
  output out_2,
  output out_3,
  output out_4,
  output out_5
);

  wire clock_1_out, j_k_ff_1_qn, j_k_ff_2_qn, j_k_ff_3_qn, not_1_out;

  Clock clock_1 (.out(clock_1_out));
  J_K_Flip_Flop j_k_ff_1 (
    .J(in_1), .K(not_1_out), .clk(clock_1_out), .Q(out_2), .Qn(j_k_ff_1_qn));  // open: preset, reset
  not not_1 (not_1_out, in_1);
  J_K_Flip_Flop j_k_ff_2 (
    .J(out_2), .K(j_k_ff_1_qn), .clk(clock_1_out), .Q(out_3), .Qn(j_k_ff_2_qn));  // open: preset, reset
  J_K_Flip_Flop j_k_ff_3 (
    .J(out_3), .K(j_k_ff_2_qn), .clk(clock_1_out), .Q(out_4), .Qn(j_k_ff_3_qn));  // open: preset, reset
  J_K_Flip_Flop j_k_ff_4 (.J(out_4), .K(j_k_ff_3_qn), .clk(clock_1_out), .Q(out_5));  // open: Qn, preset, reset
endmodule
