// Logisim project wokwi.circ as structural Verilog: 1 circuit, main circuit main
module main (
  input  in_1,
  input  in_2,
  input  in_3,
  input  in_4,
  input  in_5,
  input  in_6
);

  wire clock_1_out, d_ff_1_q, d_ff_2_q, d_ff_3_q, d_ff_4_q, multiplexer_1_out, multiplexer_2_out,
       multiplexer_3_out, multiplexer_4_out;

  Clock clock_1 (.out(clock_1_out));
  Multiplexer #(.enable("false")) multiplexer_1 (.in0(in_1), .in1(d_ff_1_q), .out(multiplexer_1_out), .sel(in_5));
  D_Flip_Flop d_ff_1 (.D(multiplexer_1_out), .clk(clock_1_out), .Q(d_ff_1_q), .reset(in_6));  // open: Qn, preset
  Multiplexer #(.enable("false")) multiplexer_2 (.in0(in_2), .in1(d_ff_2_q), .out(multiplexer_2_out), .sel(in_5));
  D_Flip_Flop d_ff_2 (.D(multiplexer_2_out), .clk(clock_1_out), .Q(d_ff_2_q), .reset(in_6));  // open: Qn, preset
  Multiplexer #(.enable("false")) multiplexer_3 (.in0(in_3), .in1(d_ff_3_q), .out(multiplexer_3_out), .sel(in_5));
  D_Flip_Flop d_ff_3 (.D(multiplexer_3_out), .clk(clock_1_out), .Q(d_ff_3_q), .reset(in_6));  // open: Qn, preset
  Multiplexer #(.enable("false")) multiplexer_4 (.in0(in_4), .in1(d_ff_4_q), .out(multiplexer_4_out), .sel(in_5));
  D_Flip_Flop d_ff_4 (.D(multiplexer_4_out), .clk(clock_1_out), .Q(d_ff_4_q), .reset(in_6));  // open: Qn, preset
endmodule
